// Logisim project 2_Boolean_Arithmetic.circ as structural Verilog: 2 circuits, main circuit main
module main (
  input  in_1,
  input  a,
  input  Input,
  input  in_4,
  input  b,
  input  in_6,
  input  in_7,
  input  a_2,
  input  in_9,
  input  in_10,
  input  in_11,
  input  in_12,
  input  in_13,
  input  in_14,
  input  in_15,
  input  in_16,
  input  in_17,
  input  in_18,
  input  in_19,
  input  in_20,
  input  in_21,
  input  in_22,
  input  in_23,
  input  b_2,
  input  in_25,
  input  in_26,
  input  in_27,
  input  in_28,
  input  in_29,
  input  in_30,
  input  in_31,
  input  in_32,
  input  in_33,
  input  in_34,
  input  in_35,
  input  in_36,
  input  in_37,
  input  in_38,
  input  in_39,
  output Output,
  output out_41,
  output out_42,
  output out_43,
  output Output_2,
  output out_45,
  output out_46,
  output out_47,
  output out_48,
  output out_49,
  output out_50,
  output out_51,
  output out_52,
  output out_53,
  output out_54,
  output out_55,
  output out_56,
  output out_57,
  output out_58,
  output out_59
);

  wire full_adder_1_cout, full_adder_2_cout, full_adder_4_sum, full_adder_5_sum1, full_adder_6_cout;

  Full_Adder full_adder_1 (.a(a), .b(b), .cin(in_1), .sum(Output), .cout(full_adder_1_cout));  // open: sum1
  Full_Adder full_adder_2 (
    .a(Input), .b(in_6), .cin(full_adder_1_cout), .sum(out_41), .cout(full_adder_2_cout));  // open: sum1
  Full_Adder full_adder_3 (.a(in_4), .b(in_7), .cin(full_adder_2_cout), .sum(out_42), .cout(out_43));  // open: sum1
  Full_Adder full_adder_4 (.a(in_9), .b(in_10), .cin(in_25), .sum(full_adder_4_sum), .cout(out_46));  // open: sum1
  Full_Adder full_adder_5 (.sum1(full_adder_5_sum1));  // open: a, b, cin, sum, cout
  Full_Adder full_adder_6 (
    .a(a_2), .b(b_2), .cin(in_10), .sum(full_adder_5_sum1), .cout(full_adder_6_cout));  // open: sum1
  Full_Adder full_adder_7 ();  // open: a, b, cin, sum1, sum, cout
  Full_Adder full_adder_8 ();  // open: a, b, cin, sum1, sum, cout
  Full_Adder full_adder_9 ();  // open: a, b, cin, sum1, sum, cout
  Full_Adder full_adder_10 ();  // open: a, b, cin, sum1, sum, cout
  Full_Adder full_adder_11 ();  // open: a, b, cin, sum1, sum, cout
  Full_Adder full_adder_12 ();  // open: a, b, cin, sum1, sum, cout
  Full_Adder full_adder_13 ();  // open: a, b, cin, sum1, sum, cout
  Full_Adder full_adder_14 ();  // open: a, b, cin, sum1, sum, cout
  Full_Adder full_adder_15 ();  // open: a, b, cin, sum1, sum, cout
  Full_Adder full_adder_16 ();  // open: a, b, cin, sum1, sum, cout
  Full_Adder full_adder_17 ();  // open: a, b, cin, sum1, sum, cout
  Full_Adder full_adder_18 ();  // open: a, b, cin, sum1, sum, cout
  Full_Adder full_adder_19 ();  // open: a, b, cin, sum1, sum, cout
  Full_Adder full_adder_20 ();  // open: a, b, cin, sum1, sum, cout
  buf xor_1 (Output_2, full_adder_5_sum1);  // XOR_Gate
  xor xor_2 (out_45, full_adder_4_sum, full_adder_6_cout);

  // Notes on the sheet:
  //   Input
  //   carry-in (ignored)
  //   carry-out (ignored)
  //   Full-Adder
  //   Bitwise AND
endmodule

module Full_Adder (
  input  a,
  input  b,
  input  cin,
  output sum1,
  output sum,
  output cout
);

  wire and_1_out, and_2_out;

  xor xor_1 (sum1, a, b);
  and and_1 (and_1_out, a, b);
  xor xor_2 (sum, sum1, cin);
  and and_2 (and_2_out, sum1, cin);
  or or_1 (cout, and_1_out, and_2_out);

  // Notes on the sheet:
  //   Input
  //   Bitwise XOR
  //   Bitwise AND
  //   Bitwise XOR
  //   Bitwise AND
  //   carry1
  //   carry2
  //   Output
endmodule
